# Fritzing sketch Sensore_Ultrasuoni_1 (saved by Fritzing 0.9.0b)
circuit board: 8.46667cm x 5.64444cm
breadboards: 1

parts:
  Componente1 = SRF05 Ultrasonic Rangefinder [part_number=HC-SR04]
  Componente2 = Arduino Uno (Rev3)

nets:
  VCC: Componente1.VCC, Componente2.5V
  N1: Componente1.Trig, Componente2.D8
  N2: Componente1.Echo, Componente2.D9_PWM
  GND: Componente1.GND, Componente2.GND
